// Logisim project ex5.circ as structural Verilog: 5 circuits, main circuit RotLeft
module RotLeft (
  input  [15:0] INPUT0,
  input  [3:0] AMOUNT,
  output [15:0] out_3
);

  wire [15:0] multiplexer_1_out, multiplexer_2_out, multiplexer_3_out, shiftleft2_1_out_2,
       shiftleft4_1_out_2, shiftleft8_1_out_2, shiftleft_1_out_2;

  Multiplexer #(.enable("false"), .width(16)) multiplexer_1 (
    .in0(INPUT0), .in1(shiftleft8_1_out_2), .out(multiplexer_1_out), .sel(AMOUNT[3]));
  ShiftLeft8 shiftleft8_1 (.in_1(INPUT0), .out_2(shiftleft8_1_out_2));
  Multiplexer #(.enable("false"), .width(16)) multiplexer_2 (
    .in0(multiplexer_1_out), .in1(shiftleft4_1_out_2), .out(multiplexer_2_out), .sel(AMOUNT[2]));
  ShiftLeft4 shiftleft4_1 (.in_1(multiplexer_1_out), .out_2(shiftleft4_1_out_2));
  ShiftLeft2 shiftleft2_1 (.in_1(multiplexer_2_out), .out_2(shiftleft2_1_out_2));
  Multiplexer #(.enable("false"), .width(16)) multiplexer_3 (
    .in0(multiplexer_2_out), .in1(shiftleft2_1_out_2), .out(multiplexer_3_out), .sel(AMOUNT[1]));
  ShiftLeft shiftleft_1 (.in_1(multiplexer_3_out), .out_2(shiftleft_1_out_2));
  Multiplexer #(.enable("false"), .width(16)) multiplexer_4 (
    .in0(multiplexer_3_out), .in1(shiftleft_1_out_2), .out(out_3), .sel(AMOUNT[0]));
endmodule

module ShiftLeft (
  input  [15:0] in_1,
  output [15:0] out_2
);


  assign out_2 = {in_1[14:0], in_1[15]};
endmodule

module ShiftLeft2 (
  input  [15:0] in_1,
  output [15:0] out_2
);

  wire [15:0] shiftleft_1_out_2;

  ShiftLeft shiftleft_1 (.in_1(in_1), .out_2(shiftleft_1_out_2));
  ShiftLeft shiftleft_2 (.in_1(shiftleft_1_out_2), .out_2(out_2));
endmodule

module ShiftLeft4 (
  input  [15:0] in_1,
  output [15:0] out_2
);

  wire [15:0] shiftleft2_1_out_2;

  ShiftLeft2 shiftleft2_1 (.in_1(in_1), .out_2(shiftleft2_1_out_2));
  ShiftLeft2 shiftleft2_2 (.in_1(shiftleft2_1_out_2), .out_2(out_2));
endmodule

module ShiftLeft8 (
  input  [15:0] in_1,
  output [15:0] out_2
);

  wire [15:0] shiftleft4_1_out_2;

  ShiftLeft4 shiftleft4_1 (.in_1(in_1), .out_2(shiftleft4_1_out_2));
  ShiftLeft4 shiftleft4_2 (.in_1(shiftleft4_1_out_2), .out_2(out_2));
endmodule
